# Fritzing sketch remote-sketch (saved by Fritzing 0.7.12b)
breadboards: 1

parts:
  Part1 = Thumb Joystick
  Part2 = Thumb Joystick
  R1 = Resistor [tolerance=±5% resistance=10k package=THT]
  Arduino1 = Arduino
  R2 = Resistor [tolerance=±5% resistance=10k package=THT]
  S1 = Pushbutton [package="[THT]"]
  R3 = Resistor [tolerance=±5% resistance=10k package=THT]

nets:
  GND: Part1.GND, Part2.GND, Arduino1.GND, R3.Pin_1
  N1: Part1.SEL, R1.Pin_0, Arduino1.D9
  N2: Part1.HORZ, Arduino1.A1
  N3: Part1.VERT, Arduino1.A0
  VCC: Part1.VCC, Part2.VCC, R1.Pin_1, Arduino1.+5V, R2.Pin_1, S1.Pin_1, S1.Pin_2
  N4: Part2.SEL, Arduino1.D10, R2.Pin_0
  N5: Part2.HORZ, Arduino1.A3
  N6: Part2.VERT, Arduino1.A2
  N7: Arduino1.D8, S1.Pin_3, S1.Pin_4, R3.Pin_0

notes:
  Joysticks are wired upside down so the cables don't get in the way on the breadboard.
  This means that up/down & left/right are reversed!
  The select button on the joystick uses a pull-up resistor.
  Johnny-Five uses buttons with pull-down resistors, so `up` is actually `down` & vice-versa.
